// Logisim project LAB 5 BCD adder circuit.circ as structural Verilog: 4 circuits, main circuit main
module main (
  input  Cin,
  input  B1,
  input  B2,
  input  B3,
  input  B4,
  input  A1,
  input  A2,
  input  A3,
  input  A4,
  input  _0,
  output S1,
  output S2,
  output S3,
  output S4,
  output Cout_ignored,
  output C__BCD_carry
);

  wire ic_74283_1_cout, ic_74283_1_s1, ic_74283_1_s2, ic_74283_1_s3, ic_74283_1_s4, n4081_and_1_out_9,
       n4081_and_1_out_11, n7432_or_1_out_12;

  _7432_OR u_7432_or_1 (
    .in_5(ic_74283_1_cout), .in_6(n7432_or_1_out_12), .in_7(n4081_and_1_out_9), .in_8(n4081_and_1_out_11),
    .out_11(C__BCD_carry), .out_12(n7432_or_1_out_12));  // open: in_1, in_2, in_3, in_4, out_9, out_10
  IC_74283 ic_74283_1 (
    .Cin(Cin), .A1(A1), .B1(B1), .A2(A2), .B2(B2), .A3(A3), .B3(B3), .A4(A4), .B4(B4), .S1(ic_74283_1_s1),
    .S2(ic_74283_1_s2), .S3(ic_74283_1_s3), .S4(ic_74283_1_s4), .Cout(ic_74283_1_cout));
  _4081_And u_4081_and_1 (
    .in_1(ic_74283_1_s3), .in_2(ic_74283_1_s4), .in_5(ic_74283_1_s2), .in_6(ic_74283_1_s4),
    .out_9(n4081_and_1_out_9), .out_11(n4081_and_1_out_11));  // open: in_3, in_4, in_7, in_8, out_10, out_12
  IC_74283 ic_74283_2 (
    .Cin(Cin), .A1(_0), .B1(ic_74283_1_s1), .A2(C__BCD_carry), .B2(ic_74283_1_s2), .A3(C__BCD_carry),
    .B3(ic_74283_1_s3), .A4(_0), .B4(ic_74283_1_s4), .S1(S1), .S2(S2), .S3(S3), .S4(S4), .Cout(Cout_ignored));

  // Notes on the sheet:
  //   Cout
  //   S1
  //   S2
  //   S3
  //   S4
  //   4081 
  //   A1
  //   A2
  //   A3
  //   A4
  //   B1
  //   B2
  //   B3
  //   B4
endmodule

module IC_74283 (
  input  Cin,
  input  A1,
  input  B1,
  input  A2,
  input  B2,
  input  A3,
  input  B3,
  input  A4,
  input  B4,
  output S1,
  output S2,
  output S3,
  output S4,
  output Cout
);

  wire adder_1_cout, adder_2_cout, adder_3_cout, xor_1_out, xor_2_out, xor_3_out, xor_4_out;

  xor xor_1 (xor_1_out, B1, Cin);
  xor xor_2 (xor_2_out, B2, Cin);
  xor xor_3 (xor_3_out, B3, Cin);
  xor xor_4 (xor_4_out, B4, Cin);
  Adder #(.width(1)) adder_1 (.a(A1), .b(xor_1_out), .out(S1), .cin(Cin), .cout(adder_1_cout));
  Adder #(.width(1)) adder_2 (.a(A2), .b(xor_2_out), .out(S2), .cin(adder_1_cout), .cout(adder_2_cout));
  Adder #(.width(1)) adder_3 (.a(A3), .b(xor_3_out), .out(S3), .cin(adder_2_cout), .cout(adder_3_cout));
  Adder #(.width(1)) adder_4 (.a(A4), .b(xor_4_out), .out(S4), .cin(adder_3_cout), .cout(Cout));
endmodule

module _4081_And (
  input  in_1,
  input  in_2,
  input  in_3,
  input  in_4,
  input  in_5,
  input  in_6,
  input  in_7,
  input  in_8,
  output out_9,
  output out_10,
  output out_11,
  output out_12
);

  and and_1 (out_9, in_1, in_2);
  and and_2 (out_10, in_3, in_4);
  and and_3 (out_11, in_5, in_6);
  and and_4 (out_12, in_7, in_8);
endmodule

module _7432_OR (
  input  in_1,
  input  in_2,
  input  in_3,
  input  in_4,
  input  in_5,
  input  in_6,
  input  in_7,
  input  in_8,
  output out_9,
  output out_10,
  output out_11,
  output out_12
);

  or or_1 (out_9, in_1, in_2);
  or or_2 (out_10, in_3, in_4);
  or or_3 (out_11, in_5, in_6);
  or or_4 (out_12, in_7, in_8);
endmodule
