// Logisim project digital circuit lab 4.circ as structural Verilog: 4 circuits, main circuit main
module main (
  input  W,
  input  X,
  input  Y,
  input  Z,
  output D,
  output B,
  output C,
  output A
);

  wire n4081_and_1_out_9, n4081_and_1_out_10, n4081_and_1_out_11, n4081_and_1_out_12, n4081_and_2_out_9,
       n4081_and_2_out_10, n4081_and_2_out_11, n7404_not_1_out_7, n7404_not_1_out_8, n7432_or_1_out_9,
       n7432_or_2_out_9;

  _7404_not u_7404_not_1 (
    .in_1(X), .in_2(Y), .in_3(Z), .out_7(n7404_not_1_out_7), .out_8(n7404_not_1_out_8), .out_9(D));  // open: in_4, in_5, in_6, out_10, out_11, out_12
  _4081_and u_4081_and_1 (
    .in_1(Z), .in_2(n7404_not_1_out_7), .in_3(n7404_not_1_out_7), .in_4(Y), .in_5(n7404_not_1_out_8),
    .in_6(D), .in_7(D), .in_8(n4081_and_1_out_10), .out_9(n4081_and_1_out_9), .out_10(n4081_and_1_out_10),
    .out_11(n4081_and_1_out_11), .out_12(n4081_and_1_out_12));
  _4081_and u_4081_and_2 (
    .in_1(X), .in_2(Y), .in_3(Y), .in_4(Z), .in_5(X), .in_6(Z), .out_9(n4081_and_2_out_9),
    .out_10(n4081_and_2_out_10), .out_11(n4081_and_2_out_11));  // open: in_7, in_8, out_12
  _7432_OR u_7432_or_1 (
    .in_1(n4081_and_2_out_9), .in_2(n4081_and_2_out_11), .in_3(n7432_or_1_out_9), .in_4(W),
    .out_9(n7432_or_1_out_9), .out_10(A));  // open: in_5, in_6, in_7, in_8, out_11, out_12
  _7432_OR u_7432_or_2 (
    .in_1(n4081_and_1_out_10), .in_2(n4081_and_1_out_12), .in_3(n7432_or_2_out_9), .in_4(n4081_and_1_out_9),
    .in_5(n4081_and_2_out_10), .in_6(n4081_and_1_out_11), .out_9(n7432_or_2_out_9), .out_10(B), .out_11(C));  // open: in_7, in_8, out_12

  // Notes on the sheet:
  //   Z'
  //   X'
  //   Y'
  //   XY
  //   X'Y
  //   X'Z
  //   XZ
  //   Y'Z'
endmodule

module _7404_not (
  input  in_1,
  input  in_2,
  input  in_3,
  input  in_4,
  input  in_5,
  input  in_6,
  output out_7,
  output out_8,
  output out_9,
  output out_10,
  output out_11,
  output out_12
);

  not not_1 (out_7, in_1);
  not not_2 (out_8, in_2);
  not not_3 (out_9, in_3);
  not not_4 (out_10, in_4);
  not not_5 (out_11, in_5);
  not not_6 (out_12, in_6);
endmodule

module _4081_and (
  input  in_1,
  input  in_2,
  input  in_3,
  input  in_4,
  input  in_5,
  input  in_6,
  input  in_7,
  input  in_8,
  output out_9,
  output out_10,
  output out_11,
  output out_12
);

  and and_1 (out_9, in_1, in_2);
  and and_2 (out_10, in_3, in_4);
  and and_3 (out_11, in_5, in_6);
  and and_4 (out_12, in_7, in_8);
endmodule

module _7432_OR (
  input  in_1,
  input  in_2,
  input  in_3,
  input  in_4,
  input  in_5,
  input  in_6,
  input  in_7,
  input  in_8,
  output out_9,
  output out_10,
  output out_11,
  output out_12
);

  or or_1 (out_9, in_1, in_2);
  or or_2 (out_10, in_3, in_4);
  or or_3 (out_11, in_5, in_6);
  or or_4 (out_12, in_7, in_8);
endmodule
